# Fritzing sketch Schema Elettrico (saved by Fritzing 0.9.3b)
breadboards: 1

parts:
  Componente1 = Arduino Uno (Rev3)
  R1 = Rotary Potentiometer (Small) [maximum_resistance=100kΩ package=THT]
  Componente2 = LED Matrix - Serial Interface - Red/Green/Blue
  S1 = Pushbutton [package="[THT]"]
  R2 = Resistor [tolerance=±5% resistance=220 package=THT]
  LED1 = LED - 5mm [color="Blue (505nm)" package="5 mm [THT]"]
  R3 = Rotary Potentiometer (Small) [maximum_resistance=100kΩ package=THT]

nets:
  N1: Componente1.A0, R1.wiper
  N2: Componente1.A1, R3.wiper
  N3: Componente1.D2, LED1.anode
  N4: Componente1.D4, Componente2.CS
  N5: Componente1.D5_PWM, Componente2.SCK
  5V: Componente1.D6_PWM, Componente1.5V, R1.leg2, Componente2.VCC, S1.Pin_3, S1.Pin_4, R3.leg2
  N6: Componente1.D7, S1.Pin_1, S1.Pin_2, R2.Pin_0
  GND: Componente1.GND, R1.leg1, Componente2.GND, R2.Pin_1, LED1.cathode, R3.leg1
